// Logisim project gap.circ as structural Verilog: 3 circuits, main circuit main
module main (
  input  SLCT,
  input  PCO,
  input  CLR,
  input  CE,
  input  J
);

  wire clock_1_out, not_1_out, not_2_out;
  wire [3:0] m_c_s_1_j_2, transistor_1_out;
  wire [15:0] pc_1__0___lsb_2, transistor_2_out;

  Clock clock_1 (.out(clock_1_out));
  Transistor #(.gate("br"), .width(4)) transistor_1 (.in(m_c_s_1_j_2), .out(transistor_1_out), .gate(not_1_out));
  not not_1 (not_1_out, SLCT);
  pc pc_1 (
    ._0___LSB(transistor_2_out[0]), ._1(transistor_2_out[1]), ._2(transistor_2_out[2]),
    ._3(transistor_2_out[3]), ._4(transistor_2_out[4]), ._5(transistor_2_out[5]), ._6(transistor_2_out[6]),
    ._7(transistor_2_out[7]), ._8(transistor_2_out[8]), ._9(transistor_2_out[9]), ._10(transistor_2_out[10]),
    ._11(transistor_2_out[11]), ._12(transistor_2_out[12]), ._13(transistor_2_out[13]),
    ._14(transistor_2_out[14]), ._15___msb(transistor_2_out[15]), ._0___LSB_2(pc_1__0___lsb_2[0]),
    ._1_2(pc_1__0___lsb_2[1]), ._2_2(pc_1__0___lsb_2[2]), ._3_2(pc_1__0___lsb_2[3]),
    ._4_2(pc_1__0___lsb_2[4]), ._5_2(pc_1__0___lsb_2[5]), ._6_2(pc_1__0___lsb_2[6]),
    ._7_2(pc_1__0___lsb_2[7]), ._8_2(pc_1__0___lsb_2[8]), ._9_2(pc_1__0___lsb_2[9]),
    ._10_2(pc_1__0___lsb_2[10]), ._11_2(pc_1__0___lsb_2[11]), ._12_2(pc_1__0___lsb_2[12]),
    ._13_2(pc_1__0___lsb_2[13]), ._14_2(pc_1__0___lsb_2[14]), ._15___msb_2(pc_1__0___lsb_2[15]),
    .J(transistor_1_out[0]), .CE(transistor_1_out[1]), .CLR(transistor_1_out[2]), .CLK(clock_1_out));
  not not_2 (not_2_out, transistor_1_out[3]);
  M_C_S m_c_s_1 (
    .J(J), .J_2(m_c_s_1_j_2[0]), .SEL(SLCT), .CE_2(m_c_s_1_j_2[1]), .CE(CE), .CLR_2(m_c_s_1_j_2[2]),
    .CLR(CLR), .PCO_2(m_c_s_1_j_2[3]), .PCO(PCO));
  Transistor #(.width(16)) transistor_2 (.in(pc_1__0___lsb_2), .out(transistor_2_out), .gate(not_2_out));
endmodule

module pc (
  input  J,
  input  CE,
  input  CLR,
  input  CLK,
  input  _0___LSB,
  input  _1,
  input  _2,
  input  _3,
  input  _4,
  input  _5,
  input  _6,
  input  _7,
  input  _8,
  input  _9,
  input  _10,
  input  _11,
  input  _12,
  input  _13,
  input  _14,
  input  _15___msb,
  output _0___LSB_2,
  output _1_2,
  output _2_2,
  output _3_2,
  output _4_2,
  output _5_2,
  output _6_2,
  output _7_2,
  output _8_2,
  output _9_2,
  output _10_2,
  output _11_2,
  output _12_2,
  output _13_2,
  output _14_2,
  output _15___msb_2
);

  wire dip_74161_1_p7, dip_74161_2_p9, dip_74161_3_p9, not_1_out, not_2_out;

  not not_1 (not_1_out, J);
  not not_2 (not_2_out, CLR);
  // DIP_74161 dip_74161_1: pin names not known; wires that end beside it: not_2_out, CLK, _0___LSB, _1, _2, _3, dip_74161_1_p7, _0___LSB_2, _1_2, _2_2, _3_2
  // DIP_74161 dip_74161_2: pin names not known; wires that end beside it: not_2_out, dip_74161_1_p7, _4, _5, _6, _7, CE, not_1_out, dip_74161_2_p9, _4_2, _5_2, _6_2, _7_2
  // DIP_74161 dip_74161_3: pin names not known; wires that end beside it: not_2_out, dip_74161_2_p9, _8, _9, _10, _11, CE, not_1_out, dip_74161_3_p9, _8_2, _9_2, _10_2, _11_2
  // DIP_74161 dip_74161_4: pin names not known; wires that end beside it: not_2_out, dip_74161_3_p9, _12, _13, _14, _15___msb, CE, not_1_out, _12_2, _13_2, _14_2, _15___msb_2, CE, not_1_out
endmodule

module M_C_S (
  input  SEL,
  input  J,
  input  CE,
  input  CLR,
  input  PCO,
  output J_2,
  output CE_2,
  output CLR_2,
  output PCO_2
);

  and and_1 (J_2, SEL, J);
  and and_2 (CE_2, SEL, CE);
  and and_3 (CLR_2, SEL, CLR);
  and and_4 (PCO_2, SEL, PCO);
endmodule
